# Fritzing sketch MP1_Diagram (saved by Fritzing 0.9.5d)
breadboards: 1

parts:
  Part1 = Arduino Leonardo (Rev3b)
  LED1 = RGB LED (com. cathode, rgb) [package="5 mm [THT]"]
  S1 = SWITCH-MOMENTARY-2 [package=tactile-pth-12mm]
  R1 = Photocell (LDR) [package=THT]
  R2 = TRIMPOT [package=3386u]
  Part2 = Breakout Board for Electret Microphone
  R3 = Resistor [tolerance=±1% resistance=10k package="2010 [SMD]"]
  R4 = Resistor [tolerance=±1% resistance=220 package="2010 [SMD]"]
  R6 = Resistor [tolerance=±1% resistance=220 package="2010 [SMD]"]
  R5 = Resistor [tolerance=±1% resistance=220 package="2010 [SMD]"]

nets:
  N1: Part1.D2/SDA, Part1.SDA, S1.1
  N2: Part1.D3_PWM/SCL, R4.Pin_0
  N3: Part1.D5_PWM, R5.Pin_0
  N4: Part1.D6_PWM/A7, R6.Pin_0
  3V3: Part1.3V3, Part2.VCC
  N5: Part1.5V, R1.pin_0, R2.CW
  N6: Part1.A0, R1.pin_1, R3.Pin_0
  N7: Part1.A1, R2.WIPER
  N8: Part1.A2, Part2.AUD
  GND: Part1.GND, LED1.common_cathode, S1.2, R2.CCW, Part2.GND, R3.Pin_1
  N9: LED1.red_anode, R4.Pin_1
  N10: LED1.green_anode, R5.Pin_1
  N11: LED1.blue_anode, R6.Pin_1
